// Logisim project cpu.circ as structural Verilog: 1 circuit, main circuit main
module main (
  input  [31:0] INSTRUCTION,
  input  CLOCK,
  output [31:0] PROGRAM_COUNTER,
  output [31:0] ra,
  output [31:0] sp,
  output [31:0] t0,
  output [31:0] t1,
  output [31:0] t2,
  output [31:0] s0,
  output [31:0] s1,
  output [31:0] a0
);

  wire [31:0] adder_1_out, ALU_result, immediate, INSTRUCTION_DELAY, PROGRAM_COUNTER_DELAY, ReadData, rs1Val,
       wb;

  // control_logic control_logic_1: pin names not known
  Adder #(.width(32)) adder_1 (.a(PROGRAM_COUNTER), .b(32'h4), .out(adder_1_out));  // open: cin, cout
  Register #(.width(32)) PC (.D(adder_1_out), .clk(CLOCK), .Q(PROGRAM_COUNTER));  // open: en, clr
  imm_gen imm_gen_1 (.inst(INSTRUCTION_DELAY), .imm(immediate));  // open: ImmSel
  Register #(.width(32)) register_1 (.D(PROGRAM_COUNTER), .clk(CLOCK), .Q(PROGRAM_COUNTER_DELAY));  // open: en, clr
  Register #(.width(32)) register_2 (.D(INSTRUCTION), .clk(CLOCK), .Q(INSTRUCTION_DELAY));  // open: en, clr
  // branch_comp branch_comp_1: pin names not known
  regfile_main RegFile (
    .rd(INSTRUCTION_DELAY[11:7]), .Read_Data_1(rs1Val), .ra(ra), .sp(sp), .t0(t0), .t1(t1), .t2(t2), .s0(s0),
    .s1(s1), .a0(a0), .rs1(INSTRUCTION_DELAY[19:15]), .Write_Data(wb), .RegWEn(1'b1), .clk(CLOCK));  // open: rs2, Read_Data_2
  alu Arithmetic_Logic_Unit (.ALUSel(4'b0000), .Result(ALU_result), .A(rs1Val), .B(immediate));
  Multiplexer #(.select(2), .width(32), .enable("false")) multiplexer_1 (
    .in1(ALU_result), .in2(ReadData), .out(wb), .sel(2'b01));  // open: in0, in3
  // mem_main DMEM: pin names not known; wires that end beside it: CLOCK, ReadData

  // Other names for the same wires on the sheet: clk = CLOCK; rd[4:0] = INSTRUCTION_DELAY[11:7];
  //   rs1Addr[4:0] = INSTRUCTION_DELAY[19:15]

  // Notes on the sheet:
  //   Output
  //   IMEM (do **NOT** move this)
  //   Inputs
  //   Inputs/Outputs for testing. Do **NOT** move these.
endmodule
