// Logisim project imm_gen.circ as structural Verilog: 1 circuit, main circuit imm_gen
module imm_gen (
  input  [31:0] inst,
  input  [2:0] ImmSel,
  output [31:0] imm
);

  wire [31:0] imm_I, imm_S, imm_SB, imm_U, imm_UJ;

  assign imm_I = {{20{inst[31]}}, inst[31:20]};  // Bit_Extender bit_extender_1
  assign imm_S = {{20{inst[31]}}, {inst[31:25], inst[11:7]}};  // Bit_Extender bit_extender_2
  assign imm_U = {{12{inst[31]}}, inst[31:12]};  // Bit_Extender bit_extender_3
  assign imm_SB = {{19{inst[31]}}, {inst[31], inst[8], inst[30:25], inst[12:9], 1'b0}};  // Bit_Extender bit_extender_4
  assign imm_UJ = {{11{inst[31]}}, {inst[31:12], 1'b0}};  // Bit_Extender bit_extender_5
  Multiplexer #(.select(3), .width(32), .enable("false")) multiplexer_1 (
    .in0({32{1'b0}}), .in1(imm_I), .in2(imm_S), .in3(imm_SB), .in4(imm_U), .in5(imm_UJ), .out(imm),
    .sel(ImmSel));  // open: in6, in7

  // Notes on the sheet:
  //   INPUTS to your circuit
  //   DON'T CHANGE THE LOCATIONS OF THE INPUTS AND OUTPUTS!
  //   OUTPUT from your circuit
endmodule
