// Logisim project regfile.circ as structural Verilog: 1 circuit, main circuit main
module main (
  input  [4:0] rs1,
  input  [4:0] rs2,
  input  [4:0] rd,
  input  [31:0] Write_Data,
  input  RegWEn,
  input  clk,
  output [31:0] ra,
  output [31:0] sp,
  output [31:0] t0,
  output [31:0] t1,
  output [31:0] t2,
  output [31:0] s0,
  output [31:0] s1,
  output [31:0] a0,
  output [31:0] Read_Data_1,
  output [31:0] Read_Data_2
);

  wire a0Write, raWrite, s0Write, s1Write, spWrite, t0Write, t1Write, t2Write;
  wire [31:0] demultiplexer_1_out1, demultiplexer_1_out2, demultiplexer_1_out5, demultiplexer_1_out6,
       demultiplexer_1_out7, demultiplexer_1_out8, demultiplexer_1_out9, demultiplexer_1_out10;

  Demultiplexer #(.select(4), .width(32), .enable("false")) demultiplexer_1 (
    .out1(demultiplexer_1_out1), .out2(demultiplexer_1_out2), .out5(demultiplexer_1_out5),
    .out6(demultiplexer_1_out6), .out7(demultiplexer_1_out7), .out8(demultiplexer_1_out8),
    .out9(demultiplexer_1_out9), .out10(demultiplexer_1_out10), .in(Write_Data), .sel(rd[3:0]));  // open: out0, out3, out4, out11, out12, out13, out14, out15
  Register #(.width(32)) register_1 (.D(demultiplexer_1_out1), .en(raWrite), .clk(clk), .Q(ra));  // open: clr
  Register #(.width(32)) register_2 (.D(demultiplexer_1_out2), .en(spWrite), .clk(clk), .Q(sp));  // open: clr
  Register #(.width(32)) register_3 (.D(demultiplexer_1_out5), .en(t0Write), .clk(clk), .Q(t0));  // open: clr
  Register #(.width(32)) register_4 (.D(demultiplexer_1_out6), .en(t1Write), .clk(clk), .Q(t1));  // open: clr
  Register #(.width(32)) register_5 (.D(demultiplexer_1_out7), .en(t2Write), .clk(clk), .Q(t2));  // open: clr
  Register #(.width(32)) register_6 (.D(demultiplexer_1_out8), .en(s0Write), .clk(clk), .Q(s0));  // open: clr
  Register #(.width(32)) register_7 (.D(demultiplexer_1_out9), .en(s1Write), .clk(clk), .Q(s1));  // open: clr
  Register #(.width(32)) register_8 (.D(demultiplexer_1_out10), .en(a0Write), .clk(clk), .Q(a0));  // open: clr
  Demultiplexer #(.select(4), .enable("false")) demultiplexer_2 (
    .out1(raWrite), .out2(spWrite), .out5(t0Write), .out6(t1Write), .out7(t2Write), .out8(s0Write),
    .out9(s1Write), .out10(a0Write), .in(RegWEn), .sel(rd[3:0]));  // open: out0, out3, out4, out11, out12, out13, out14, out15
  Multiplexer #(.select(4), .width(32), .enable("false")) multiplexer_1 (
    .in0({32{1'b0}}), .in1(ra), .in2(sp), .in5(t0), .in6(t1), .in7(t2), .in8(s0), .in9(s1), .in10(a0),
    .out(Read_Data_1), .sel(rs1[3:0]));  // open: in3, in4, in11, in12, in13, in14, in15
  Multiplexer #(.select(4), .width(32), .enable("false")) multiplexer_2 (
    .in0({32{1'b0}}), .in1(ra), .in2(sp), .in5(t0), .in6(t1), .in7(t2), .in8(s0), .in9(s1), .in10(a0),
    .out(Read_Data_2), .sel(rs2[3:0]));  // open: in3, in4, in11, in12, in13, in14, in15

  // Other names for the same wires on the sheet: read_data1[31:0] = Read_Data_1; read_data2[31:0] = Read_Data_2;
  //   read_reg1[4:0] = rs1; read_reg1_3_0[3:0] = rs1[3:0]; read_reg2[4:0] = rs2; read_reg2_3_0[3:0] = rs2[3:0];
  //   write_en = RegWEn; write_reg[4:0] = rd; write_reg3_0[3:0] = rd[3:0]

  // Notes on the sheet:
  //   INPUTS to your circuit
  //   These are DEBUG/TEST outputs from your circuit.
  //   OUTPUTS from your circuit
endmodule
